// Logisim project NC16.circ as structural Verilog: 2 circuits, main circuit main
module main (
);

  wire adder_1_cout, and_1_out, and_2_out, and_3_out, and_4_out, clock_1_out, d_ff_1_q, d_ff_2_q,
       decoder_1_out0, decoder_1_out1, decoder_1_out2, decoder_1_out3, decoder_1_out4, decoder_1_out5,
       decoder_1_out6, decoder_1_out7, decoder_1_out8, multiplexer_8_out, not_1_out, not_2_out, not_3_out,
       not_4_out, not_6_out, not_7_out, not_8_out, not_10_out, not_11_out, not_12_out, not_13_out,
       not_14_out, not_15_out, not_16_out, not_17_out, not_18_out, not_19_out, not_20_out, not_21_out,
       not_22_out, not_23_out, not_24_out, not_25_out, RESET_out;
  wire [0:0] not_5_out;
  wire [1:0] counter_1_q;
  wire [2:0] one_out, shift_register_1_p6, subtractor_1_bout;
  wire [3:0] Instruction_Decorder_out_2;
  wire [7:0] Output_port_q, Output_port_q_2;
  wire [13:0] pla_1_out;
  wire [15:0] A_q, adder_1_out, and_6_out, B_q, BP_q, C_q, D_q, demultiplexer_1_out0, demultiplexer_1_out1,
       demultiplexer_2_out0, demultiplexer_2_out1, demultiplexer_2_out2, demultiplexer_2_out3,
       demultiplexer_2_out4, demultiplexer_2_out5, demultiplexer_2_out6, demultiplexer_2_out7,
       demultiplexer_3_out0, demultiplexer_3_out1, demultiplexer_3_out2, demultiplexer_3_out3,
       demultiplexer_3_out4, demultiplexer_3_out6, demultiplexer_3_out7, E_q, multiplexer_1_out,
       multiplexer_2_out, multiplexer_3_out, multiplexer_4_out, multiplexer_5_out, multiplexer_6_out,
       multiplexer_7_out, multiplexer_9_out, multiplexer_10_out, multiplexer_11_out, multiplexer_12_out,
       multiplexer_13_out, multiplexer_15_out, multiplexer_16_out, multiplexer_17_out, multiplier_1_cout,
       multiplier_1_out, not_9_out, or_1_out, PC_q, ram_1_dout, register_1_q, shift_register_1_p3,
       shift_register_1_p4, shift_register_1_p5, SP_q, subtractor_1_out, undriven, xor_1_out;
  wire [15:3] FLAGS_q;
  wire [18:0] Instruction_Decorder_out;
  wire [19:16] and_5_out;

  DipSwitch #(.number(15)) Input_data ();  // open: sw1, sw2, sw3, sw4, sw5, sw6, sw7, sw8, sw9, sw10, sw11, sw12, sw13, sw14, sw15
  LED INPUT_WAIT (.in(Output_port_q_2[7]));
  Button three (.out(one_out[2]));
  Button two (.out(one_out[1]));
  LED CPU_THINKING (.in(Output_port_q_2[6]));
  Clock clock_1 (.out(clock_1_out));
  Button one (.out(one_out[0]));
  LED CPU_WIN (.in(Output_port_q_2[5]));
  and and_1 (and_1_out, clock_1_out, not_8_out);
  Button RESET (.out(RESET_out));
  Decoder #(.select(4)) decoder_1 (
    .out0(decoder_1_out0), .out1(decoder_1_out1), .out2(decoder_1_out2), .out3(decoder_1_out3),
    .out4(decoder_1_out4), .out5(decoder_1_out5), .out6(decoder_1_out6), .out7(decoder_1_out7),
    .out8(decoder_1_out8), .sel(Instruction_Decorder_out[6:3]));  // open: out9, out10, out11, out12, out13, out14, out15, en
  LED HUMAN_WIN (.in(Output_port_q_2[4]));
  PLA #(.in_width(8), .out_width(14), .\table ("00000000 01111110111111 # 00\n00000001 00001100111111 # 01\n00000010 10110110111111 # 02\n00000011 10011110111111 # 03\n00000100 11001100111111 # 04\n00000101 11011010111111 # 05\n00000110 11111010111111 # 06\n00000111 00001110111111 # 07\n00001000 11111110111111 # 08\n00001001 11011110111111 # 09\n00001010 01111110000110 # 10\n00001011 00001100000110 # 11\n00001100 10110110000110 # 12\n00001101 10011110000110 # 13\n00001110 11001100000110 # 14\n00001111 11011010000110 # 15\n00010000 11111010000110 # 16\n00010001 00001110000110 # 17\n00010010 11111110000110 # 18\n00010011 11011110000110 # 19\n00010100 01111111011011 # 20\n00010101 00001101011011 # 21\n00010110 10110111011011 # 22\n00010111 10011111011011 # 23\n00011000 11001101011011 # 24\n00011001 11011011011011 # 25\n00011010 11111011011011 # 26\n00011011 00001111011011 # 27\n00011100 11111111011011 # 28\n00011101 11011111011011 # 29\n00011110 01111111001111 # 30\n00011111 00001101001111 # 31\n00100000 10110111001111 # 32\n00100001 10011111001111 # 33\n00100010 11001101001111 # 34\n00100011 11011011001111 # 35\n00100100 11111011001111 # 36\n00100101 00001111001111 # 37\n00100110 11111111001111 # 38\n00100111 11011111001111 # 39\n00101000 01111111100110 # 40\n00101001 00001101100110 # 41\n00101010 10110111100110 # 42\n00101011 10011111100110 # 43\n00101100 11001101100110 # 44\n00101101 11011011100110 # 45\n00101110 11111011100110 # 46\n00101111 00001111100110 # 47\n00110000 11111111100110 # 48\n00110001 11011111100110 # 49\n00110010 01111111101101 # 50\n00110011 00001101101101 # 51\n00110100 10110111101101 # 52\n00110101 10011111101101 # 53\n00110110 11001101101101 # 54\n00110111 11011011101101 # 55\n00111000 11111011101101 # 56\n00111001 00001111101101 # 57\n00111010 11111111101101 # 58\n00111011 11011111101101 # 59\n00111100 01111111111101 # 60\n00111101 00001101111101 # 61\n00111110 10110111111101 # 62\n00111111 10011111111101 # 63\n01000000 11001101111101 # 64\n01000001 11011011111101 # 65\n01000010 11111011111101 # 66\n01000011 00001111111101 # 67\n01000100 11111111111101 # 68\n01000101 11011111111101 # 69\n01000110 01111110000111 # 70\n01000111 00001100000111 # 71\n01001000 10110110000111 # 72\n01001001 10011110000111 # 73\n01001010 11001100000111 # 74\n01001011 11011010000111 # 75\n01001100 11111010000111 # 76\n01001101 00001110000111 # 77\n01001110 11111110000111 # 78\n01001111 11011110000111 # 79\n01010000 01111111111111 # 80\n01010001 00001101111111 # 81\n01010010 10110111111111 # 82\n01010011 10011111111111 # 83\n01010100 11001101111111 # 84\n01010101 11011011111111 # 85\n01010110 11111011111111 # 86\n01010111 00001111111111 # 87\n01011000 11111111111111 # 88\n01011001 11011111111111 # 89\n01011010 01111111101111 # 90\n01011011 00001101101111 # 91\n01011100 10110111101111 # 92\n01011101 10011111101111 # 93\n01011110 11001101101111 # 94\n01011111 11011011101111 # 95\n01100000 11111011101111 # 96\n01100001 00001111101111 # 97\n01100010 11111111101111 # 98\n01100011 11011111101111 # 99")) pla_1 (
    .in(Output_port_q), .out(pla_1_out));
  LedBar #(.matrixcols(16)) ledbar_1 (
    .led0(multiplexer_15_out[15]), .led1(multiplexer_15_out[14]), .led2(multiplexer_15_out[13]),
    .led3(multiplexer_15_out[12]), .led4(multiplexer_15_out[11]), .led5(multiplexer_15_out[10]),
    .led6(multiplexer_15_out[9]), .led7(multiplexer_15_out[8]), .led8(multiplexer_15_out[7]),
    .led9(multiplexer_15_out[6]), .led10(multiplexer_15_out[5]), .led11(multiplexer_15_out[4]),
    .led12(multiplexer_15_out[3]), .led13(multiplexer_15_out[2]), .led14(multiplexer_15_out[1]),
    .led15(multiplexer_15_out[0]));
  Multiplexer #(.width(16)) multiplexer_1 (
    .in0(A_q), .in1(multiplexer_15_out), .out(multiplexer_1_out), .sel(decoder_1_out0));
  Multiplexer #(.width(16)) multiplexer_2 (
    .in0(B_q), .in1(multiplexer_15_out), .out(multiplexer_2_out), .sel(decoder_1_out1));
  Multiplexer #(.width(16)) multiplexer_3 (
    .in0(C_q), .in1(multiplexer_15_out), .out(multiplexer_3_out), .sel(decoder_1_out2));
  Multiplexer #(.width(16)) multiplexer_4 (
    .in0(D_q), .in1(multiplexer_15_out), .out(multiplexer_4_out), .sel(decoder_1_out3));
  Multiplexer #(.width(16)) multiplexer_5 (
    .in0(E_q), .in1(multiplexer_15_out), .out(multiplexer_5_out), .sel(decoder_1_out4));
  Multiplexer #(.width(16)) multiplexer_6 (
    .in0(BP_q), .in1(multiplexer_15_out), .out(multiplexer_6_out), .sel(decoder_1_out5));
  Multiplexer #(.width(16)) multiplexer_7 (
    .in0(SP_q), .in1(multiplexer_15_out), .out(multiplexer_7_out), .sel(decoder_1_out6));
  Multiplexer multiplexer_8 (.in0(decoder_1_out7), .in1(1'b1), .out(multiplexer_8_out), .sel(and_2_out));
  and and_2 (and_2_out, d_ff_1_q, not_1_out);
  not not_1 (not_1_out, not_2_out);
  Multiplexer #(.width(16)) multiplexer_9 (
    .in0({Output_port_q_2, Output_port_q}), .in1(multiplexer_15_out), .out(multiplexer_9_out),
    .sel(decoder_1_out8));
  _7_Segment_Display u_7_segment_display_1 (
    .g(pla_1_out[6]), .f(pla_1_out[5]), .a(pla_1_out[0]), .b(pla_1_out[1]), .e(pla_1_out[4]),
    .d(pla_1_out[3]), .c(pla_1_out[2]));  // open: dp
  Register #(.width(16)) A (.D(multiplexer_1_out), .en(decoder_1_out0), .clk(and_1_out), .Q(A_q), .clr(RESET_out));
  Register #(.width(16)) B (.D(multiplexer_2_out), .en(decoder_1_out1), .clk(and_1_out), .Q(B_q), .clr(RESET_out));
  Register #(.width(16)) C (.D(multiplexer_3_out), .en(decoder_1_out2), .clk(and_1_out), .Q(C_q), .clr(RESET_out));
  Register #(.width(16)) D (.D(multiplexer_4_out), .en(decoder_1_out3), .clk(and_1_out), .Q(D_q), .clr(RESET_out));
  Register #(.width(16)) E (.D(multiplexer_5_out), .en(decoder_1_out4), .clk(and_1_out), .Q(E_q), .clr(RESET_out));
  Register #(.width(16)) BP (.D(multiplexer_6_out), .en(decoder_1_out5), .clk(and_1_out), .Q(BP_q), .clr(RESET_out));
  Register #(.width(16)) SP (.D(multiplexer_7_out), .en(decoder_1_out6), .clk(and_1_out), .Q(SP_q), .clr(RESET_out));
  Counter #(.max('hffff), .width(16)) PC (
    .clr(RESET_out), .load(multiplexer_8_out), .clk(and_1_out), .D(multiplexer_11_out), .Q(PC_q));  // open: up, count, carry
  Multiplexer #(.width(16)) multiplexer_10 (
    .in0(PC_q), .in1(multiplexer_15_out), .out(multiplexer_10_out), .sel(multiplexer_8_out));
  Multiplexer #(.width(16)) multiplexer_11 (
    .in0(multiplexer_10_out), .in1(register_1_q), .out(multiplexer_11_out), .sel(and_2_out));
  Register #(.width(16)) Output_port (
    .D(multiplexer_9_out), .en(decoder_1_out8), .clk(and_1_out), .Q({Output_port_q_2, Output_port_q}),
    .clr(RESET_out));
  LedBar #(.matrixcols(16)) ledbar_2 (
    .led0(Output_port_q_2[7]), .led1(Output_port_q_2[6]), .led2(Output_port_q_2[5]),
    .led3(Output_port_q_2[4]), .led4(Output_port_q_2[3]), .led5(Output_port_q_2[2]),
    .led6(Output_port_q_2[1]), .led7(Output_port_q_2[0]), .led8(Output_port_q[7]), .led9(Output_port_q[6]),
    .led10(Output_port_q[5]), .led11(Output_port_q[4]), .led12(Output_port_q[3]), .led13(Output_port_q[2]),
    .led14(Output_port_q[1]), .led15(Output_port_q[0]));
  _7_Segment_Display u_7_segment_display_2 (
    .g(pla_1_out[13]), .f(pla_1_out[12]), .a(pla_1_out[7]), .b(pla_1_out[8]), .e(pla_1_out[11]),
    .d(pla_1_out[10]), .c(pla_1_out[9]));  // open: dp
  LedBar #(.matrixcols(16)) ledbar_3 (
    .led0(PC_q[15]), .led1(PC_q[14]), .led2(PC_q[13]), .led3(PC_q[12]), .led4(PC_q[11]), .led5(PC_q[10]),
    .led6(PC_q[9]), .led7(PC_q[8]), .led8(PC_q[7]), .led9(PC_q[6]), .led10(PC_q[5]), .led11(PC_q[4]),
    .led12(PC_q[3]), .led13(PC_q[2]), .led14(PC_q[1]), .led15(PC_q[0]));
  Register #(.width(16)) register_1 (.D(PC_q), .en(1'b1), .clk(and_1_out), .Q(register_1_q), .clr(RESET_out));
  not not_2 (not_2_out, and_3_out);
  and and_3 (and_3_out, not_3_out, not_4_out);
  D_Flip_Flop d_ff_1 (.D(not_2_out), .clk(and_1_out), .Q(d_ff_1_q), .reset(RESET_out));  // open: Qn, preset
  not not_3 (not_3_out, Instruction_Decorder_out[1]);
  not not_4 (not_4_out, Instruction_Decorder_out[2]);
  Multiplexer #(.select(2), .width(16)) multiplexer_12 (
    .in0(PC_q), .in1(A_q), .in2(shift_register_1_p4), .out(multiplexer_12_out),
    .sel(Instruction_Decorder_out[2:1]));  // open: in3
  RAM #(.addrWidth(16), .dataWidth(16), .enables("line")) ram_1 (
    .addr(multiplexer_12_out), .we(Instruction_Decorder_out[0]), .clk(and_1_out), .din(B_q), .dout(ram_1_dout));
  LedBar #(.matrixcols(16)) ledbar_4 (
    .led0(demultiplexer_1_out0[15]), .led1(demultiplexer_1_out0[14]), .led2(demultiplexer_1_out0[13]),
    .led3(demultiplexer_1_out0[12]), .led4(demultiplexer_1_out0[11]), .led5(demultiplexer_1_out0[10]),
    .led6(demultiplexer_1_out0[9]), .led7(demultiplexer_1_out0[8]), .led8(demultiplexer_1_out0[7]),
    .led9(demultiplexer_1_out0[6]), .led10(demultiplexer_1_out0[5]), .led11(demultiplexer_1_out0[4]),
    .led12(demultiplexer_1_out0[3]), .led13(demultiplexer_1_out0[2]), .led14(demultiplexer_1_out0[1]),
    .led15(demultiplexer_1_out0[0]));
  Multiplexer #(.select(4), .width(16)) multiplexer_13 (
    .in0(A_q), .in1(B_q), .in2(C_q), .in3(D_q), .in4(E_q), .in5(BP_q), .in6(SP_q), .in7(shift_register_1_p4),
    .in8({{13{1'b0}}, one_out}), .in9(ram_1_dout), .in10(PC_q), .out(multiplexer_13_out),
    .sel(Instruction_Decorder_out_2));  // open: in11, in12, in13, in14, in15
  // Shift_Register #(.length(2), .width(16)) shift_register_1: pin names not known; wires that end beside it: RESET_out, and_1_out, shift_register_1_p3, shift_register_1_p4, shift_register_1_p5, shift_register_1_p6, shift_register_1_p6
  Multiplexer #(.width(16)) multiplexer_14 (
    .in0(ram_1_dout), .in1({16{1'b1}}), .out(shift_register_1_p3), .sel(not_2_out));
  Counter #(.max('h3), .width(2)) counter_1 (
    .clr(RESET_out), .load(and_5_out[16]), .clk(and_1_out), .D({1'b0, not_5_out[0]}), .Q(counter_1_q));  // open: up, count, carry
  Multiplexer #(.width(16)) multiplexer_15 (
    .in0(demultiplexer_1_out0), .in1(multiplexer_17_out), .out(multiplexer_15_out),
    .sel(Instruction_Decorder_out[13]));
  Demultiplexer #(.width(16)) demultiplexer_1 (
    .out0(demultiplexer_1_out0), .out1(demultiplexer_1_out1), .in(multiplexer_13_out),
    .sel(Instruction_Decorder_out[13]));
  not not_5 (not_5_out[0], and_4_out);
  Demultiplexer #(.select(3), .width(16)) demultiplexer_2 (
    .out0(demultiplexer_2_out0), .out1(demultiplexer_2_out1), .out2(demultiplexer_2_out2),
    .out3(demultiplexer_2_out3), .out4(demultiplexer_2_out4), .out5(demultiplexer_2_out5),
    .out6(demultiplexer_2_out6), .out7(demultiplexer_2_out7), .in(demultiplexer_1_out1),
    .sel(Instruction_Decorder_out[9:7]));
  and and_4 (and_4_out, Instruction_Decorder_out[3], Instruction_Decorder_out[4], Instruction_Decorder_out[5], not_6_out);
  not not_6 (not_6_out, Instruction_Decorder_out[6]);
  Multiplexer #(.select(3), .width(16)) multiplexer_16 (
    .in0(A_q), .in1(B_q), .in2(C_q), .in3(D_q), .in4(E_q), .in5(BP_q), .in6(SP_q), .in7(shift_register_1_p4),
    .out(multiplexer_16_out), .sel(shift_register_1_p6));
  not not_7 (not_7_out, counter_1_q[0]);
  Demultiplexer #(.select(3), .width(16)) demultiplexer_3 (
    .out0(demultiplexer_3_out0), .out1(demultiplexer_3_out1), .out2(demultiplexer_3_out2),
    .out3(demultiplexer_3_out3), .out4(demultiplexer_3_out4), .out6(demultiplexer_3_out6),
    .out7(demultiplexer_3_out7), .in(multiplexer_16_out), .sel(Instruction_Decorder_out[9:7]));  // open: out5
  and and_5 (and_5_out[16], not_7_out, counter_1_q[1]);
  LED Instruction_Execute (.in(and_5_out[16]));
  PLA #(.in_width(20), .out_width(19), .\table ("xxx0xxxxxxxxxxxxxxxx 0000000000001111000 # IE=0 (during fetch)\n00x10000101111111111 0011100000000111000 # jnc opd (Taken)\n10x10000101111111111 0000000000001111000 # jnc opd (Skip)\n10x10000110011111111 0011100000000111000 # jc opd (Taken)\n00x10000110011111111 0000000000001111000 # jc opd (Skip)\nx0x10000110111111111 0011100000000111000 # jnz opd (Taken)\nx1x10000110111111111 0000000000001111000 # jnz opd (Skip)\nx1x10000111011111111 0011100000000111000 # jz opd (Taken)\nx0x10000111011111111 0000000000001111000 # jz opd (Skip)\nxx010000111111111111 0011100000000111000 # jns opd (Taken)\nxx110000111111111111 0000000000001111000 # jns opd (Skip)\nxx110001000011111111 0011100000000111000 # js opd (Taken)\nxx010001000011111111 0000000000001111000 # js opd (Skip)\nxxx10001000111111111 0011100000000111000 # jmp opd\nx1x10001011011111111 0011100000000111000 # je opd (Taken)\nx0x10001011011111111 0000000000001111000 # je opd (Skip)\nx0x10001011111111111 0011100000000111000 # jne opd(Taken)\nx1x10001011111111111 0000000000001111000 # jne opd(Skip)\nx0010001100011111111 0011100000000111000 # ja opd (Taken)\nxxx10001100011111111 0000000000001111000 # ja opd (Skip)\nx0010001100111111111 0011100000000111000 # jae opd (Taken)\nx1010001100111111111 0011100000000111000 # jae opd (Taken)\nxxx10001100111111111 0000000000001111000 # jae opd (Skip)\nx0110001101011111111 0011100000000111000 # jl opd (Taken)\nxxx10001101011111111 0000000000001111000 # jl opd (Skip)\nx0110001101111111111 0011100000000111000 # jle opd (Taken)\nx1010001101111111111 0011100000000111000 # jle opd (Taken)\nxxx10001101111111111 0000000000001111000 # jle opd (Skip)\nxxx10000100001110001 0000100000001111011 # mov [a], b\nxxx10000100001110001 0000100000001111101 # mov [opd], b\nxxx10001001111111111 1000000000001111000 # hlt\nxxx10001010011111111 0000000000001111000 # nop\nxxxx1111111111111111 0000000000001111000 # invaild\nxxx10001010111111111 0101000000000000000 # lpc\nxxx10000000000000000 0000010000000000000 # add a, a\nxxx10000000000000001 0000010010000000000 # add a, b\nxxx10000000000000010 0000010100000000000 # add a, c\nxxx10000000000000011 0000010110000000000 # add a, d\nxxx10000000000000100 0000011000000000000 # add a, e\nxxx10000000000000101 0000011010000000000 # add a, bp\nxxx10000000000000110 0000011100000000000 # add a, sp\nxxx10000000000010000 0000110000000001000 # add b, a\nxxx10000000000010001 0000110010000001000 # add b, b\nxxx10000000000010010 0000110100000001000 # add b, c\nxxx10000000000010011 0000110110000001000 # add b, d\nxxx10000000000010100 0000111000000001000 # add b, e\nxxx10000000000010101 0000111010000001000 # add b, bp\nxxx10000000000010110 0000111100000001000 # add b, sp\nxxx10000000000100000 0001010000000010000 # add c, a\nxxx10000000000100001 0001010010000010000 # add c, b\nxxx10000000000100010 0001010100000010000 # add c, c\nxxx10000000000100011 0001010110000010000 # add c, d\nxxx10000000000100100 0001011000000010000 # add c, e\nxxx10000000000100101 0001011010000010000 # add c, bp\nxxx10000000000100110 0001011100000010000 # add c, sp\nxxx10000000000110000 0001110000000011000 # add d, a\nxxx10000000000110001 0001110010000011000 # add d, b\nxxx10000000000110010 0001110100000011000 # add d, c\nxxx10000000000110011 0001110110000011000 # add d, d\nxxx10000000000110100 0001111000000011000 # add d, e\nxxx10000000000110101 0001111010000011000 # add d, bp\nxxx10000000000110110 0001111100000011000 # add d, sp\nxxx10000000001000000 0010010000000100000 # add e, a\nxxx10000000001000001 0010010010000100000 # add e, b\nxxx10000000001000010 0010010100000100000 # add e, c\nxxx10000000001000011 0010010110000100000 # add e, d\nxxx10000000001000100 0010011000000100000 # add e, e\nxxx10000000001000101 0010011010000100000 # add e, bp\nxxx10000000001000110 0010011100000100000 # add e, sp\nxxx10000000001010000 0010110000000101000 # add bp, a\nxxx10000000001010001 0010110010000101000 # add bp, b\nxxx10000000001010010 0010110100000101000 # add bp, c\nxxx10000000001010011 0010110110000101000 # add bp, d\nxxx10000000001010100 0010111000000101000 # add bp, e\nxxx10000000001010101 0010111010000101000 # add bp, bp\nxxx10000000001010110 0010111100000101000 # add bp, sp\nxxx10000000001100000 0011010000000110000 # add sp, a\nxxx10000000001100001 0011010010000110000 # add sp, b\nxxx10000000001100010 0011010100000110000 # add sp, c\nxxx10000000001100011 0011010110000110000 # add sp, d\nxxx10000000001100100 0011011000000110000 # add sp, e\nxxx10000000001100101 0011011010000110000 # add sp, bp\nxxx10000000001100110 0011011100000110000 # add sp, sp\nxxx10000000100000000 0000010000010000000 # sub a, a\nxxx10000000100000001 0000010010010000000 # sub a, b\nxxx10000000100000010 0000010100010000000 # sub a, c\nxxx10000000100000011 0000010110010000000 # sub a, d\nxxx10000000100000100 0000011000010000000 # sub a, e\nxxx10000000100000101 0000011010010000000 # sub a, bp\nxxx10000000100000110 0000011100010000000 # sub a, sp\nxxx10000000100010000 0000110000010001000 # sub b, a\nxxx10000000100010001 0000110010010001000 # sub b, b\nxxx10000000100010010 0000110100010001000 # sub b, c\nxxx10000000100010011 0000110110010001000 # sub b, d\nxxx10000000100010100 0000111000010001000 # sub b, e\nxxx10000000100010101 0000111010010001000 # sub b, bp\nxxx10000000100010110 0000111100010001000 # sub b, sp\nxxx10000000100100000 0001010000010010000 # sub c, a\nxxx10000000100100001 0001010010010010000 # sub c, b\nxxx10000000100100010 0001010100010010000 # sub c, c\nxxx10000000100100011 0001010110010010000 # sub c, d\nxxx10000000100100100 0001011000010010000 # sub c, e\nxxx10000000100100101 0001011010010010000 # sub c, bp\nxxx10000000100100110 0001011100010010000 # sub c, sp\nxxx10000000100110000 0001110000010011000 # sub d, a\nxxx10000000100110001 0001110010010011000 # sub d, b\nxxx10000000100110010 0001110100010011000 # sub d, c\nxxx10000000100110011 0001110110010011000 # sub d, d\nxxx10000000100110100 0001111000010011000 # sub d, e\nxxx10000000100110101 0001111010010011000 # sub d, bp\nxxx10000000100110110 0001111100010011000 # sub d, sp\nxxx10000000101000000 0010010000010100000 # sub e, a\nxxx10000000101000001 0010010010010100000 # sub e, b\nxxx10000000101000010 0010010100010100000 # sub e, c\nxxx10000000101000011 0010010110010100000 # sub e, d\nxxx10000000101000100 0010011000010100000 # sub e, e\nxxx10000000101000101 0010011010010100000 # sub e, bp\nxxx10000000101000110 0010011100010100000 # sub e, sp\nxxx10000000101010000 0010110000010101000 # sub bp, a\nxxx10000000101010001 0010110010010101000 # sub bp, b\nxxx10000000101010010 0010110100010101000 # sub bp, c\nxxx10000000101010011 0010110110010101000 # sub bp, d\nxxx10000000101010100 0010111000010101000 # sub bp, e\nxxx10000000101010101 0010111010010101000 # sub bp, bp\nxxx10000000101010110 0010111100010101000 # sub bp, sp\nxxx10000000101100000 0011010000010110000 # sub sp, a\nxxx10000000101100001 0011010010010110000 # sub sp, b\nxxx10000000101100010 0011010100010110000 # sub sp, c\nxxx10000000101100011 0011010110010110000 # sub sp, d\nxxx10000000101100100 0011011000010110000 # sub sp, e\nxxx10000000101100101 0011011010010110000 # sub sp, bp\nxxx10000000101100110 0011011100010110000 # sub sp, sp\nxxx10000001000000000 0000010000100000000 # mul a, a\nxxx10000001000000001 0000010010100000000 # mul a, b\nxxx10000001000000010 0000010100100000000 # mul a, c\nxxx10000001000000011 0000010110100000000 # mul a, d\nxxx10000001000000100 0000011000100000000 # mul a, e\nxxx10000001000000101 0000011010100000000 # mul a, bp\nxxx10000001000000110 0000011100100000000 # mul a, sp\nxxx10000001000010000 0000110000100001000 # mul b, a\nxxx10000001000010001 0000110010100001000 # mul b, b\nxxx10000001000010010 0000110100100001000 # mul b, c\nxxx10000001000010011 0000110110100001000 # mul b, d\nxxx10000001000010100 0000111000100001000 # mul b, e\nxxx10000001000010101 0000111010100001000 # mul b, bp\nxxx10000001000010110 0000111100100001000 # mul b, sp\nxxx10000001000100000 0001010000100010000 # mul c, a\nxxx10000001000100001 0001010010100010000 # mul c, b\nxxx10000001000100010 0001010100100010000 # mul c, c\nxxx10000001000100011 0001010110100010000 # mul c, d\nxxx10000001000100100 0001011000100010000 # mul c, e\nxxx10000001000100101 0001011010100010000 # mul c, bp\nxxx10000001000100110 0001011100100010000 # mul c, sp\nxxx10000001000110000 0001110000100011000 # mul d, a\nxxx10000001000110001 0001110010100011000 # mul d, b\nxxx10000001000110010 0001110100100011000 # mul d, c\nxxx10000001000110011 0001110110100011000 # mul d, d\nxxx10000001000110100 0001111000100011000 # mul d, e\nxxx10000001000110101 0001111010100011000 # mul d, bp\nxxx10000001000110110 0001111100100011000 # mul d, sp\nxxx10000001001000000 0010010000100100000 # mul e, a\nxxx10000001001000001 0010010010100100000 # mul e, b\nxxx10000001001000010 0010010100100100000 # mul e, c\nxxx10000001001000011 0010010110100100000 # mul e, d\nxxx10000001001000100 0010011000100100000 # mul e, e\nxxx10000001001000101 0010011010100100000 # mul e, bp\nxxx10000001001000110 0010011100100100000 # mul e, sp\nxxx10000001001010000 0010110000100101000 # mul bp, a\nxxx10000001001010001 0010110010100101000 # mul bp, b\nxxx10000001001010010 0010110100100101000 # mul bp, c\nxxx10000001001010011 0010110110100101000 # mul bp, d\nxxx10000001001010100 0010111000100101000 # mul bp, e\nxxx10000001001010101 0010111010100101000 # mul bp, bp\nxxx10000001001010110 0010111100100101000 # mul bp, sp\nxxx10000001001100000 0011010000100110000 # mul sp, a\nxxx10000001001100001 0011010010100110000 # mul sp, b\nxxx10000001001100010 0011010100100110000 # mul sp, c\nxxx10000001001100011 0011010110100110000 # mul sp, d\nxxx10000001001100100 0011011000100110000 # mul sp, e\nxxx10000001001100101 0011011010100110000 # mul sp, bp\nxxx10000001001100110 0011011100100110000 # mul sp, sp\nxxx10000001100000000 0000010000110000000 # and a, a\nxxx10000001100000001 0000010010110000000 # and a, b\nxxx10000001100000010 0000010100110000000 # and a, c\nxxx10000001100000011 0000010110110000000 # and a, d\nxxx10000001100000100 0000011000110000000 # and a, e\nxxx10000001100000101 0000011010110000000 # and a, bp\nxxx10000001100000110 0000011100110000000 # and a, sp\nxxx10000001100010000 0000110000110001000 # and b, a\nxxx10000001100010001 0000110010110001000 # and b, b\nxxx10000001100010010 0000110100110001000 # and b, c\nxxx10000001100010011 0000110110110001000 # and b, d\nxxx10000001100010100 0000111000110001000 # and b, e\nxxx10000001100010101 0000111010110001000 # and b, bp\nxxx10000001100010110 0000111100110001000 # and b, sp\nxxx10000001100100000 0001010000110010000 # and c, a\nxxx10000001100100001 0001010010110010000 # and c, b\nxxx10000001100100010 0001010100110010000 # and c, c\nxxx10000001100100011 0001010110110010000 # and c, d\nxxx10000001100100100 0001011000110010000 # and c, e\nxxx10000001100100101 0001011010110010000 # and c, bp\nxxx10000001100100110 0001011100110010000 # and c, sp\nxxx10000001100110000 0001110000110011000 # and d, a\nxxx10000001100110001 0001110010110011000 # and d, b\nxxx10000001100110010 0001110100110011000 # and d, c\nxxx10000001100110011 0001110110110011000 # and d, d\nxxx10000001100110100 0001111000110011000 # and d, e\nxxx10000001100110101 0001111010110011000 # and d, bp\nxxx10000001100110110 0001111100110011000 # and d, sp\nxxx10000001101000000 0010010000110100000 # and e, a\nxxx10000001101000001 0010010010110100000 # and e, b\nxxx10000001101000010 0010010100110100000 # and e, c\nxxx10000001101000011 0010010110110100000 # and e, d\nxxx10000001101000100 0010011000110100000 # and e, e\nxxx10000001101000101 0010011010110100000 # and e, bp\nxxx10000001101000110 0010011100110100000 # and e, sp\nxxx10000001101010000 0010110000110101000 # and bp, a\nxxx10000001101010001 0010110010110101000 # and bp, b\nxxx10000001101010010 0010110100110101000 # and bp, c\nxxx10000001101010011 0010110110110101000 # and bp, d\nxxx10000001101010100 0010111000110101000 # and bp, e\nxxx10000001101010101 0010111010110101000 # and bp, bp\nxxx10000001101010110 0010111100110101000 # and bp, sp\nxxx10000001101100000 0011010000110110000 # and sp, a\nxxx10000001101100001 0011010010110110000 # and sp, b\nxxx10000001101100010 0011010100110110000 # and sp, c\nxxx10000001101100011 0011010110110110000 # and sp, d\nxxx10000001101100100 0011011000110110000 # and sp, e\nxxx10000001101100101 0011011010110110000 # and sp, bp\nxxx10000001101100110 0011011100110110000 # and sp, sp\nxxx10000010000000000 0000010001000000000 # or a, a\nxxx10000010000000001 0000010011000000000 # or a, b\nxxx10000010000000010 0000010101000000000 # or a, c\nxxx10000010000000011 0000010111000000000 # or a, d\nxxx10000010000000100 0000011001000000000 # or a, e\nxxx10000010000000101 0000011011000000000 # or a, bp\nxxx10000010000000110 0000011101000000000 # or a, sp\nxxx10000010000010000 0000110001000001000 # or b, a\nxxx10000010000010001 0000110011000001000 # or b, b\nxxx10000010000010010 0000110101000001000 # or b, c\nxxx10000010000010011 0000110111000001000 # or b, d\nxxx10000010000010100 0000111001000001000 # or b, e\nxxx10000010000010101 0000111011000001000 # or b, bp\nxxx10000010000010110 0000111101000001000 # or b, sp\nxxx10000010000100000 0001010001000010000 # or c, a\nxxx10000010000100001 0001010011000010000 # or c, b\nxxx10000010000100010 0001010101000010000 # or c, c\nxxx10000010000100011 0001010111000010000 # or c, d\nxxx10000010000100100 0001011001000010000 # or c, e\nxxx10000010000100101 0001011011000010000 # or c, bp\nxxx10000010000100110 0001011101000010000 # or c, sp\nxxx10000010000110000 0001110001000011000 # or d, a\nxxx10000010000110001 0001110011000011000 # or d, b\nxxx10000010000110010 0001110101000011000 # or d, c\nxxx10000010000110011 0001110111000011000 # or d, d\nxxx10000010000110100 0001111001000011000 # or d, e\nxxx10000010000110101 0001111011000011000 # or d, bp\nxxx10000010000110110 0001111101000011000 # or d, sp\nxxx10000010001000000 0010010001000100000 # or e, a\nxxx10000010001000001 0010010011000100000 # or e, b\nxxx10000010001000010 0010010101000100000 # or e, c\nxxx10000010001000011 0010010111000100000 # or e, d\nxxx10000010001000100 0010011001000100000 # or e, e\nxxx10000010001000101 0010011011000100000 # or e, bp\nxxx10000010001000110 0010011101000100000 # or e, sp\nxxx10000010001010000 0010110001000101000 # or bp, a\nxxx10000010001010001 0010110011000101000 # or bp, b\nxxx10000010001010010 0010110101000101000 # or bp, c\nxxx10000010001010011 0010110111000101000 # or bp, d\nxxx10000010001010100 0010111001000101000 # or bp, e\nxxx10000010001010101 0010111011000101000 # or bp, bp\nxxx10000010001010110 0010111101000101000 # or bp, sp\nxxx10000010001100000 0011010001000110000 # or sp, a\nxxx10000010001100001 0011010011000110000 # or sp, b\nxxx10000010001100010 0011010101000110000 # or sp, c\nxxx10000010001100011 0011010111000110000 # or sp, d\nxxx10000010001100100 0011011001000110000 # or sp, e\nxxx10000010001100101 0011011011000110000 # or sp, bp\nxxx10000010001100110 0011011101000110000 # or sp, sp\nxxx10000011000000000 0000010001100000000 # xor a, a\nxxx10000011000000001 0000010011100000000 # xor a, b\nxxx10000011000000010 0000010101100000000 # xor a, c\nxxx10000011000000011 0000010111100000000 # xor a, d\nxxx10000011000000100 0000011001100000000 # xor a, e\nxxx10000011000000101 0000011011100000000 # xor a, bp\nxxx10000011000000110 0000011101100000000 # xor a, sp\nxxx10000011000010000 0000110001100001000 # xor b, a\nxxx10000011000010001 0000110011100001000 # xor b, b\nxxx10000011000010010 0000110101100001000 # xor b, c\nxxx10000011000010011 0000110111100001000 # xor b, d\nxxx10000011000010100 0000111001100001000 # xor b, e\nxxx10000011000010101 0000111011100001000 # xor b, bp\nxxx10000011000010110 0000111101100001000 # xor b, sp\nxxx10000011000100000 0001010001100010000 # xor c, a\nxxx10000011000100001 0001010011100010000 # xor c, b\nxxx10000011000100010 0001010101100010000 # xor c, c\nxxx10000011000100011 0001010111100010000 # xor c, d\nxxx10000011000100100 0001011001100010000 # xor c, e\nxxx10000011000100101 0001011011100010000 # xor c, bp\nxxx10000011000100110 0001011101100010000 # xor c, sp\nxxx10000011000110000 0001110001100011000 # xor d, a\nxxx10000011000110001 0001110011100011000 # xor d, b\nxxx10000011000110010 0001110101100011000 # xor d, c\nxxx10000011000110011 0001110111100011000 # xor d, d\nxxx10000011000110100 0001111001100011000 # xor d, e\nxxx10000011000110101 0001111011100011000 # xor d, bp\nxxx10000011000110110 0001111101100011000 # xor d, sp\nxxx10000011001000000 0010010001100100000 # xor e, a\nxxx10000011001000001 0010010011100100000 # xor e, b\nxxx10000011001000010 0010010101100100000 # xor e, c\nxxx10000011001000011 0010010111100100000 # xor e, d\nxxx10000011001000100 0010011001100100000 # xor e, e\nxxx10000011001000101 0010011011100100000 # xor e, bp\nxxx10000011001000110 0010011101100100000 # xor e, sp\nxxx10000011001010000 0010110001100101000 # xor bp, a\nxxx10000011001010001 0010110011100101000 # xor bp, b\nxxx10000011001010010 0010110101100101000 # xor bp, c\nxxx10000011001010011 0010110111100101000 # xor bp, d\nxxx10000011001010100 0010111001100101000 # xor bp, e\nxxx10000011001010101 0010111011100101000 # xor bp, bp\nxxx10000011001010110 0010111101100101000 # xor bp, sp\nxxx10000011001100000 0011010001100110000 # xor sp, a\nxxx10000011001100001 0011010011100110000 # xor sp, b\nxxx10000011001100010 0011010101100110000 # xor sp, c\nxxx10000011001100011 0011010111100110000 # xor sp, d\nxxx10000011001100100 0011011001100110000 # xor sp, e\nxxx10000011001100101 0011011011100110000 # xor sp, bp\nxxx10000011001100110 0011011101100110000 # xor sp, sp\nxxx10000011100000000 0000010001110000000 # div a, a\nxxx10000011100000001 0000010011110000000 # div a, b\nxxx10000011100000010 0000010101110000000 # div a, c\nxxx10000011100000011 0000010111110000000 # div a, d\nxxx10000011100000100 0000011001110000000 # div a, e\nxxx10000011100000101 0000011011110000000 # div a, bp\nxxx10000011100000110 0000011101110000000 # div a, sp\nxxx10000011100010000 0000110001110001000 # div b, a\nxxx10000011100010001 0000110011110001000 # div b, b\nxxx10000011100010010 0000110101110001000 # div b, c\nxxx10000011100010011 0000110111110001000 # div b, d\nxxx10000011100010100 0000111001110001000 # div b, e\nxxx10000011100010101 0000111011110001000 # div b, bp\nxxx10000011100010110 0000111101110001000 # div b, sp\nxxx10000011100100000 0001010001110010000 # div c, a\nxxx10000011100100001 0001010011110010000 # div c, b\nxxx10000011100100010 0001010101110010000 # div c, c\nxxx10000011100100011 0001010111110010000 # div c, d\nxxx10000011100100100 0001011001110010000 # div c, e\nxxx10000011100100101 0001011011110010000 # div c, bp\nxxx10000011100100110 0001011101110010000 # div c, sp\nxxx10000011100110000 0001110001110011000 # div d, a\nxxx10000011100110001 0001110011110011000 # div d, b\nxxx10000011100110010 0001110101110011000 # div d, c\nxxx10000011100110011 0001110111110011000 # div d, d\nxxx10000011100110100 0001111001110011000 # div d, e\nxxx10000011100110101 0001111011110011000 # div d, bp\nxxx10000011100110110 0001111101110011000 # div d, sp\nxxx10000011101000000 0010010001110100000 # div e, a\nxxx10000011101000001 0010010011110100000 # div e, b\nxxx10000011101000010 0010010101110100000 # div e, c\nxxx10000011101000011 0010010111110100000 # div e, d\nxxx10000011101000100 0010011001110100000 # div e, e\nxxx10000011101000101 0010011011110100000 # div e, bp\nxxx10000011101000110 0010011101110100000 # div e, sp\nxxx10000011101010000 0010110001110101000 # div bp, a\nxxx10000011101010001 0010110011110101000 # div bp, b\nxxx10000011101010010 0010110101110101000 # div bp, c\nxxx10000011101010011 0010110111110101000 # div bp, d\nxxx10000011101010100 0010111001110101000 # div bp, e\nxxx10000011101010101 0010111011110101000 # div bp, bp\nxxx10000011101010110 0010111101110101000 # div bp, sp\nxxx10000011101100000 0011010001110110000 # div sp, a\nxxx10000011101100001 0011010011110110000 # div sp, b\nxxx10000011101100010 0011010101110110000 # div sp, c\nxxx10000011101100011 0011010111110110000 # div sp, d\nxxx10000011101100100 0011011001110110000 # div sp, e\nxxx10000011101100101 0011011011110110000 # div sp, bp\nxxx10000011101100110 0011011101110110000 # div sp, sp\nxxx10000000000001111 0000011110000000000 # add a, opd\nxxx10000000000011111 0000111110000001000 # add b, opd\nxxx10000000000101111 0001011110000010000 # add c, opd\nxxx10000000000111111 0001111110000011000 # add d, opd\nxxx10000000001001111 0010011110000100000 # add e, opd\nxxx10000000001011111 0010111110000101000 # add bp, opd\nxxx10000000001101111 0011011110000110000 # add sp, opd\nxxx10000000100001111 0000011110010000000 # sub a, opd\nxxx10000000100011111 0000111110010001000 # sub b, opd\nxxx10000000100101111 0001011110010010000 # sub c, opd\nxxx10000000100111111 0001111110010011000 # sub d, opd\nxxx10000000101001111 0010011110010100000 # sub e, opd\nxxx10000000101011111 0010111110010101000 # sub bp, opd\nxxx10000000101101111 0011011110010110000 # sub sp, opd\nxxx10000001000001111 0000011110100000000 # mul a, opd\nxxx10000001000011111 0000111110100001000 # mul b, opd\nxxx10000001000101111 0001011110100010000 # mul c, opd\nxxx10000001000111111 0001111110100011000 # mul d, opd\nxxx10000001001001111 0010011110100100000 # mul e, opd\nxxx10000001001011111 0010111110100101000 # mul bp, opd\nxxx10000001001101111 0011011110100110000 # mul sp, opd\nxxx10000001100001111 0000011110110000000 # and a, opd\nxxx10000001100011111 0000111110110001000 # and b, opd\nxxx10000001100101111 0001011110110010000 # and c, opd\nxxx10000001100111111 0001111110110011000 # and d, opd\nxxx10000001101001111 0010011110110100000 # and e, opd\nxxx10000001101011111 0010111110110101000 # and bp, opd\nxxx10000001101101111 0011011110110110000 # and sp, opd\nxxx10000010000001111 0000011111000000000 # or a, opd\nxxx10000010000011111 0000111111000001000 # or b, opd\nxxx10000010000101111 0001011111000010000 # or c, opd\nxxx10000010000111111 0001111111000011000 # or d, opd\nxxx10000010001001111 0010011111000100000 # or e, opd\nxxx10000010001011111 0010111111000101000 # or bp, opd\nxxx10000010001101111 0011011111000110000 # or sp, opd\nxxx10000011000001111 0000011111100000000 # xor a, opd\nxxx10000011000011111 0000111111100001000 # xor b, opd\nxxx10000011000101111 0001011111100010000 # xor c, opd\nxxx10000011000111111 0001111111100011000 # xor d, opd\nxxx10000011001001111 0010011111100100000 # xor e, opd\nxxx10000011001011111 0010111111100101000 # xor bp, opd\nxxx10000011001101111 0011011111100110000 # xor sp, opd\nxxx10000011100001111 0000011111110000000 # div a, opd\nxxx10000011100011111 0000111111110001000 # div b, opd\nxxx10000011100101111 0001011111110010000 # div c, opd\nxxx10000011100111111 0001111111110011000 # div d, opd\nxxx10000011101001111 0010011111110100000 # div e, opd\nxxx10000011101011111 0010111111110101000 # div bp, opd\nxxx10000011101101111 0011011111110110000 # div sp, opd\nxxx10000000000000111 0100010000000000010 # add a, [a]\nxxx10000000000010111 0100010010000001010 # add b, [a]\nxxx10000000000100111 0100010100000010010 # add c, [a]\nxxx10000000000110111 0100010110000011010 # add d, [a]\nxxx10000000001000111 0100011000000100010 # add e, [a]\nxxx10000000001010111 0100011010000101010 # add bp, [a]\nxxx10000000001100111 0100011100000110010 # add sp, [a]\nxxx10000000100000111 0100010000010000010 # sub a, [a]\nxxx10000000100010111 0100010010010001010 # sub b, [a]\nxxx10000000100100111 0100010100010010010 # sub c, [a]\nxxx10000000100110111 0100010110010011010 # sub d, [a]\nxxx10000000101000111 0100011000010100010 # sub e, [a]\nxxx10000000101010111 0100011010010101010 # sub bp, [a]\nxxx10000000101100111 0100011100010110010 # sub sp, [a]\nxxx10000001000000111 0100010000100000010 # mul a, [a]\nxxx10000001000010111 0100010010100001010 # mul b, [a]\nxxx10000001000100111 0100010100100010010 # mul c, [a]\nxxx10000001000110111 0100010110100011010 # mul d, [a]\nxxx10000001001000111 0100011000100100010 # mul e, [a]\nxxx10000001001010111 0100011010100101010 # mul bp, [a]\nxxx10000001001100111 0100011100100110010 # mul sp, [a]\nxxx10000001100000111 0100010000110000010 # and a, [a]\nxxx10000001100010111 0100010010110001010 # and b, [a]\nxxx10000001100100111 0100010100110010010 # and c, [a]\nxxx10000001100110111 0100010110110011010 # and d, [a]\nxxx10000001101000111 0100011000110100010 # and e, [a]\nxxx10000001101010111 0100011010110101010 # and bp, [a]\nxxx10000001101100111 0100011100110110010 # and sp, [a]\nxxx10000010000000111 0100010001000000010 # or a, [a]\nxxx10000010000010111 0100010011000001010 # or b, [a]\nxxx10000010000100111 0100010101000010010 # or c, [a]\nxxx10000010000110111 0100010111000011010 # or d, [a]\nxxx10000010001000111 0100011001000100010 # or e, [a]\nxxx10000010001010111 0100011011000101010 # or bp, [a]\nxxx10000010001100111 0100011101000110010 # or sp, [a]\nxxx10000011000000111 0100010001100000010 # sub a, [a]\nxxx10000011000010111 0100010011100001010 # sub b, [a]\nxxx10000011000100111 0100010101100010010 # sub c, [a]\nxxx10000011000110111 0100010111100011010 # sub d, [a]\nxxx10000011001000111 0100011001100100010 # sub e, [a]\nxxx10000011001010111 0100011011100101010 # sub bp, [a]\nxxx10000011001100111 0100011101100110010 # sub sp, [a]\nxxx10000011100000111 0100010001110000010 # div a, [a]\nxxx10000011100010111 0100010011110001010 # div b, [a]\nxxx10000011100100111 0100010101110010010 # div c, [a]\nxxx10000011100110111 0100010111110011010 # div d, [a]\nxxx10000011101000111 0100011001110100010 # div e, [a]\nxxx10000011101010111 0100011011110101010 # div bp, [a]\nxxx10000011101100111 0100011101110110010 # div sp, [a]\nxxx10000010100001111 0000010001010000000 # not a\nxxx10000010100011111 0000110001010001000 # not b\nxxx10000010100101111 0001010001010010000 # not c\nxxx10000010100111111 0001110001010011000 # not d\nxxx10000010101001111 0010010001010100000 # not e\nxxx10000010101011111 0010110001010101000 # not bp\nxxx10000010101101111 0011010001010110000 # not sp\nxxx10000100000000000 0000000000000000000 # mov a, a\nxxx10000100000000001 0000100000000000000 # mov a, b\nxxx10000100000000010 0001000000000000000 # mov a, c\nxxx10000100000000011 0001100000000000000 # mov a, d\nxxx10000100000000100 0010000000000000000 # mov a, e\nxxx10000100000000101 0010100000000000000 # mov a, bp\nxxx10000100000000110 0011000000000000000 # mov a, sp\nxxx10000100000010000 0000000000000001000 # mov b, a\nxxx10000100000010001 0000100000000001000 # mov b, b\nxxx10000100000010010 0001000000000001000 # mov b, c\nxxx10000100000010011 0001100000000001000 # mov b, d\nxxx10000100000010100 0010000000000001000 # mov b, e\nxxx10000100000010101 0010100000000001000 # mov b, bp\nxxx10000100000010110 0011000000000001000 # mov b, sp\nxxx10000100000100000 0000000000000010000 # mov c, a\nxxx10000100000100001 0000100000000010000 # mov c, b\nxxx10000100000100010 0001000000000010000 # mov c, c\nxxx10000100000100011 0001100000000010000 # mov c, d\nxxx10000100000100100 0010000000000010000 # mov c, e\nxxx10000100000100101 0010100000000010000 # mov c, bp\nxxx10000100000100110 0011000000000010000 # mov c, sp\nxxx10000100000110000 0000000000000011000 # mov d, a\nxxx10000100000110001 0000100000000011000 # mov d, b\nxxx10000100000110010 0001000000000011000 # mov d, c\nxxx10000100000110011 0001100000000011000 # mov d, d\nxxx10000100000110100 0010000000000011000 # mov d, e\nxxx10000100000110101 0010100000000011000 # mov d, bp\nxxx10000100000110110 0011000000000011000 # mov d, sp\nxxx10000100001000000 0000000000000100000 # mov e, a\nxxx10000100001000001 0000100000000100000 # mov e, b\nxxx10000100001000010 0001000000000100000 # mov e, c\nxxx10000100001000011 0001100000000100000 # mov e, d\nxxx10000100001000100 0010000000000100000 # mov e, e\nxxx10000100001000101 0010100000000100000 # mov e, bp\nxxx10000100001000110 0011000000000100000 # mov e, sp\nxxx10000100001010000 0000000000000101000 # mov bp, a\nxxx10000100001010001 0000100000000101000 # mov bp, b\nxxx10000100001010010 0001000000000101000 # mov bp, c\nxxx10000100001010011 0001100000000101000 # mov bp, d\nxxx10000100001010100 0010000000000101000 # mov bp, e\nxxx10000100001010101 0010100000000101000 # mov bp, bp\nxxx10000100001010110 0011000000000101000 # mov bp, sp\nxxx10000100001100000 0000000000000110000 # mov sp, a\nxxx10000100001100001 0000100000000110000 # mov sp, b\nxxx10000100001100010 0001000000000110000 # mov sp, c\nxxx10000100001100011 0001100000000110000 # mov sp, d\nxxx10000100001100100 0010000000000110000 # mov sp, e\nxxx10000100001100101 0010100000000110000 # mov sp, bp\nxxx10000100001100110 0011000000000110000 # mov sp, sp\nxxx10000100000000111 0100100000000000010 # mov a, [a]\nxxx10000100000010111 0100100000000001010 # mov b, [a]\nxxx10000100000100111 0100100000000010010 # mov c, [a]\nxxx10000100000110111 0100100000000011010 # mov d, [a]\nxxx10000100001000111 0100100000000100010 # mov e, [a]\nxxx10000100001010111 0100100000000101010 # mov bp, [a]\nxxx10000100001100111 0100100000000110010 # mov sp, [a]\nxxx10000100000001111 0011100000000000000 # mov a, opd\nxxx10000100000011111 0011100000000001000 # mov b, opd\nxxx10000100000101111 0011100000000010000 # mov c, opd\nxxx10000100000111111 0011100000000011000 # mov d, opd\nxxx10000100001001111 0011100000000100000 # mov e, opd\nxxx10000100001011111 0011100000000101000 # mov bp, opd\nxxx10000100001101111 0011100000000110000 # mov sp, opd\nxxx10000100000000111 0100100000000000100 # mov a, [opd]\nxxx10000100000010111 0100100000000001100 # mov b, [opd]\nxxx10000100000100111 0100100000000010100 # mov c, [opd]\nxxx10000100000110111 0100100000000011100 # mov d, [opd]\nxxx10000100001000111 0100100000000100100 # mov e, [opd]\nxxx10000100001010111 0100100000000101100 # mov bp, [opd]\nxxx10000100001100111 0100100000000110100 # mov sp, [opd]\nxxx10000100100001111 0100000000000000000 # in a\nxxx10000100100011111 0100000000000001000 # in b\nxxx10000100100101111 0100000000000010000 # in c\nxxx10000100100111111 0100000000000011000 # in d\nxxx10000100101001111 0100000000000100000 # in e\nxxx10000100101011111 0100000000000101000 # in bp\nxxx10000100101101111 0100000000000110000 # in sp\nxxx10000101000001111 0000000000001000000 # out a\nxxx10000101000011111 0000100000001000000 # out b\nxxx10000101000101111 0001000000001000000 # out c\nxxx10000101000111111 0001100000001000000 # out d\nxxx10000101001001111 0010000000001000000 # out e\nxxx10000101001011111 0010100000001000000 # out bp\nxxx10000101001101111 0011000000001000000 # out sp\nxxx10001001000000000 0000010000011111000 # cmp a, a\nxxx10001001000000001 0000010010011111000 # cmp a, b\nxxx10001001000000010 0000010100011111000 # cmp a, c\nxxx10001001000000011 0000010110011111000 # cmp a, d\nxxx10001001000000100 0000011000011111000 # cmp a, e\nxxx10001001000000101 0000011010011111000 # cmp a, bp\nxxx10001001000000110 0000011100011111000 # cmp a, sp\nxxx10001001000010000 0000110000011111000 # cmp b, a\nxxx10001001000010001 0000110010011111000 # cmp b, b\nxxx10001001000010010 0000110100011111000 # cmp b, c\nxxx10001001000010011 0000110110011111000 # cmp b, d\nxxx10001001000010100 0000111000011111000 # cmp b, e\nxxx10001001000010101 0000111010011111000 # cmp b, bp\nxxx10001001000010110 0000111100011111000 # cmp b, sp\nxxx10001001000100000 0001010000011111000 # cmp c, a\nxxx10001001000100001 0001010010011111000 # cmp c, b\nxxx10001001000100010 0001010100011111000 # cmp c, c\nxxx10001001000100011 0001010110011111000 # cmp c, d\nxxx10001001000100100 0001011000011111000 # cmp c, e\nxxx10001001000100101 0001011010011111000 # cmp c, bp\nxxx10001001000100110 0001011100011111000 # cmp c, sp\nxxx10001001000110000 0001110000011111000 # cmp d, a\nxxx10001001000110001 0001110010011111000 # cmp d, b\nxxx10001001000110010 0001110100011111000 # cmp d, c\nxxx10001001000110011 0001110110011111000 # cmp d, d\nxxx10001001000110100 0001111000011111000 # cmp d, e\nxxx10001001000110101 0001111010011111000 # cmp d, bp\nxxx10001001000110110 0001111100011111000 # cmp d, sp\nxxx10001001001000000 0010010000011111000 # cmp e, a\nxxx10001001001000001 0010010010011111000 # cmp e, b\nxxx10001001001000010 0010010100011111000 # cmp e, c\nxxx10001001001000011 0010010110011111000 # cmp e, d\nxxx10001001001000100 0010011000011111000 # cmp e, e\nxxx10001001001000101 0010011010011111000 # cmp e, bp\nxxx10001001001000110 0010011100011111000 # cmp e, sp\nxxx10001001001010000 0010110000011111000 # cmp bp, a\nxxx10001001001010001 0010110010011111000 # cmp bp, b\nxxx10001001001010010 0010110100011111000 # cmp bp, c\nxxx10001001001010011 0010110110011111000 # cmp bp, d\nxxx10001001001010100 0010111000011111000 # cmp bp, e\nxxx10001001001010101 0010111010011111000 # cmp bp, bp\nxxx10001001001010110 0010111100011111000 # cmp bp, sp\nxxx10001001001100000 0011010000011111000 # cmp sp, a\nxxx10001001001100001 0011010010011111000 # cmp sp, b\nxxx10001001001100010 0011010100011111000 # cmp sp, c\nxxx10001001001100011 0011010110011111000 # cmp sp, d\nxxx10001001001100100 0011011000011111000 # cmp sp, e\nxxx10001001001100101 0011011010011111000 # cmp sp, bp\nxxx10001001001100110 0011011100011111000 # cmp sp, sp\nxxx10001001000001111 0000011110011111000 # cmp a, opd\nxxx10001001000011111 0000111110011111000 # cmp b, opd\nxxx10001001000101111 0001011110011111000 # cmp c, opd\nxxx10001001000111111 0001111110011111000 # cmp d, opd\nxxx10001001001001111 0010011110011111000 # cmp e, opd\nxxx10001001001011111 0010111110011111000 # cmp bp, opd\nxxx10001001001101111 0011011110011111000 # cmp sp, opd\n00x10000101100001111 0000000000000111000 # jnc opd (Taken)\n00x10000101100011111 0000100000000111000 # jnc opd (Taken)\n00x10000101100101111 0001000000000111000 # jnc opd (Taken)\n00x10000101100111111 0001100000000111000 # jnc opd (Taken)\n00x10000101101001111 0010000000000111000 # jnc opd (Taken)\n00x10000101101011111 0010100000000111000 # jnc opd (Taken)\n00x10000101101101111 0011000000000111000 # jnc opd (Taken)\n10x10000101100001111 0000000000001111000 # jnc opd (Skip)\n10x10000101100011111 0000000000001111000 # jnc opd (Skip)\n10x10000101100101111 0000000000001111000 # jnc opd (Skip)\n10x10000101100111111 0000000000001111000 # jnc opd (Skip)\n10x10000101101001111 0000000000001111000 # jnc opd (Skip)\n10x10000101101011111 0000000000001111000 # jnc opd (Skip)\n10x10000101101101111 0000000000001111000 # jnc opd (Skip)\n10x10000110000001111 0000000000000111000 # jc opd (Taken)\n10x10000110000011111 0000100000000111000 # jc opd (Taken)\n10x10000110000101111 0001000000000111000 # jc opd (Taken)\n10x10000110000111111 0001100000000111000 # jc opd (Taken)\n10x10000110001001111 0010000000000111000 # jc opd (Taken)\n10x10000110001011111 0010100000000111000 # jc opd (Taken)\n10x10000110001101111 0011000000000111000 # jc opd (Taken)\n00x10000110000001111 0000000000001111000 # jc opd (Skip)\n00x10000110000011111 0000000000001111000 # jc opd (Skip)\n00x10000110000101111 0000000000001111000 # jc opd (Skip)\n00x10000110000111111 0000000000001111000 # jc opd (Skip)\n00x10000110001001111 0000000000001111000 # jc opd (Skip)\n00x10000110001011111 0000000000001111000 # jc opd (Skip)\n00x10000110001101111 0000000000001111000 # jc opd (Skip)\nx0x10000110100001111 0000000000000111000 # jnz a (Taken)\nx0x10000110100011111 0000100000000111000 # jnz b (Taken)\nx0x10000110100101111 0001000000000111000 # jnz c (Taken)\nx0x10000110100111111 0001100000000111000 # jnz d (Taken)\nx0x10000110101001111 0010000000000111000 # jnz e (Taken)\nx0x10000110101011111 0010100000000111000 # jnz bp (Taken)\nx0x10000110101101111 0011000000000111000 # jnz sp (Taken)\nx1x10000110100001111 0000000000001111000 # jnz a (Skip)\nx1x10000110100011111 0000000000001111000 # jnz b (Skip)\nx1x10000110100101111 0000000000001111000 # jnz c (Skip)\nx1x10000110100111111 0000000000001111000 # jnz d (Skip)\nx1x10000110101001111 0000000000001111000 # jnz e (Skip)\nx1x10000110101011111 0000000000001111000 # jnz bp (Skip)\nx1x10000110101101111 0000000000001111000 # jnz sp (Skip)\nx1x10000111000001111 0000000000000111000 # jz a (Taken)\nx1x10000111000011111 0000100000000111000 # jz b (Taken)\nx1x10000111000101111 0001000000000111000 # jz c (Taken)\nx1x10000111000111111 0001100000000111000 # jz d (Taken)\nx1x10000111001001111 0010000000000111000 # jz e (Taken)\nx1x10000111001011111 0010100000000111000 # jz bp (Taken)\nx1x10000111001101111 0011000000000111000 # jz sp (Taken)\nx0x10000111000001111 0000000000001111000 # jz a (Skip)\nx0x10000111000011111 0000000000001111000 # jz b (Skip)\nx0x10000111000101111 0000000000001111000 # jz c (Skip)\nx0x10000111000111111 0000000000001111000 # jz d (Skip)\nx0x10000111001001111 0000000000001111000 # jz e (Skip)\nx0x10000111001011111 0000000000001111000 # jz bp (Skip)\nx0x10000111001101111 0000000000001111000 # jz sp (Skip)\nxx010000111100001111 0000000000000111000 # jns a (Taken)\nxx010000111100011111 0000100000000111000 # jns b (Taken)\nxx010000111100101111 0001000000000111000 # jns c (Taken)\nxx010000111100111111 0001100000000111000 # jns d (Taken)\nxx010000111101001111 0010000000000111000 # jns e (Taken)\nxx010000111101011111 0010100000000111000 # jns bp (Taken)\nxx010000111101101111 0011000000000111000 # jns sp (Taken)\nxx110000111100001111 0000000000001111000 # jns a (Skip)\nxx110000111100011111 0000000000001111000 # jns b (Skip)\nxx110000111100101111 0000000000001111000 # jns c (Skip)\nxx110000111100111111 0000000000001111000 # jns d (Skip)\nxx110000111101001111 0000000000001111000 # jns e (Skip)\nxx110000111101011111 0000000000001111000 # jns bp (Skip)\nxx110000111101101111 0000000000001111000 # jns sp (Skip)\nxx110001000000001111 0000000000000111000 # js a (Taken)\nxx110001000000011111 0000100000000111000 # js b (Taken)\nxx110001000000101111 0001000000000111000 # js c (Taken)\nxx110001000000111111 0001100000000111000 # js d (Taken)\nxx110001000001001111 0010000000000111000 # js e (Taken)\nxx110001000001011111 0010100000000111000 # js bp (Taken)\nxx110001000001101111 0011000000000111000 # js sp (Taken)\nxx010001000000001111 0000000000001111000 # js a (Skip)\nxx010001000000011111 0000000000001111000 # js b (Skip)\nxx010001000000101111 0000000000001111000 # js c (Skip)\nxx010001000000111111 0000000000001111000 # js d (Skip)\nxx010001000001001111 0000000000001111000 # js e (Skip)\nxx010001000001011111 0000000000001111000 # js bp (Skip)\nxx010001000001101111 0000000000001111000 # js sp (Skip)\nxxx10001000100001111 0000000000000111000 # jmp a\nxxx10001000100011111 0000100000000111000 # jmp b\nxxx10001000100101111 0001000000000111000 # jmp c\nxxx10001000100111111 0001100000000111000 # jmp d\nxxx10001000101001111 0010000000000111000 # jmp e\nxxx10001000101011111 0010100000000111000 # jmp bp\nxxx10001000101101111 0011000000000111000 # jmp sp\nx1x10001011000001111 0000000000000111000 # je a (Taken)\nx1x10001011000011111 0000100000000111000 # je b (Taken)\nx1x10001011000101111 0001000000000111000 # je c (Taken)\nx1x10001011000111111 0001100000000111000 # je d (Taken)\nx1x10001011001001111 0010000000000111000 # je e (Taken)\nx1x10001011001011111 0010100000000111000 # je bp (Taken)\nx1x10001011001101111 0011000000000111000 # je sp (Taken)\nx0x10001011000001111 0000000000001111000 # je a (Skip)\nx0x10001011000011111 0000000000001111000 # je b (Skip)\nx0x10001011000101111 0000000000001111000 # je c (Skip)\nx0x10001011000111111 0000000000001111000 # je d (Skip)\nx0x10001011001001111 0000000000001111000 # je e (Skip)\nx0x10001011001011111 0000000000001111000 # je bp (Skip)\nx0x10001011001101111 0000000000001111000 # je sp (Skip)\nx0x10001011100001111 0000000000000111000 # jne a(Taken)\nx0x10001011100011111 0000100000000111000 # jne b(Taken)\nx0x10001011100101111 0001000000000111000 # jne c(Taken)\nx0x10001011100111111 0001100000000111000 # jne d(Taken)\nx0x10001011101001111 0010000000000111000 # jne e(Taken)\nx0x10001011101011111 0010100000000111000 # jne bp(Taken)\nx0x10001011101101111 0011000000000111000 # jne sp(Taken)\nx1x10001011100001111 0000000000001111000 # jne a(Skip)\nx1x10001011100011111 0000000000001111000 # jne b(Skip)\nx1x10001011100101111 0000000000001111000 # jne c(Skip)\nx1x10001011100111111 0000000000001111000 # jne d(Skip)\nx1x10001011101001111 0000000000001111000 # jne e(Skip)\nx1x10001011101011111 0000000000001111000 # jne bp(Skip)\nx1x10001011101101111 0000000000001111000 # jne sp(Skip)\nx0010001100000001111 0000000000000111000 # ja a (Taken)\nx0010001100000011111 0000100000000111000 # ja b (Taken)\nx0010001100000101111 0001000000000111000 # ja c (Taken)\nx0010001100000111111 0001100000000111000 # ja d (Taken)\nx0010001100001001111 0010000000000111000 # ja e (Taken)\nx0010001100001011111 0010100000000111000 # ja bp (Taken)\nx0010001100001101111 0011000000000111000 # ja sp (Taken)\nxxx10001100000001111 0000000000001111000 # ja a (Skip)\nxxx10001100000011111 0000000000001111000 # ja b (Skip)\nxxx10001100000101111 0000000000001111000 # ja c (Skip)\nxxx10001100000111111 0000000000001111000 # ja d (Skip)\nxxx10001100001001111 0000000000001111000 # ja e (Skip)\nxxx10001100001011111 0000000000001111000 # ja bp (Skip)\nxxx10001100001101111 0000000000001111000 # ja sp (Skip)\nx0010001100100001111 0000000000000111000 # jae a (Taken)\nx0010001100100011111 0000100000000111000 # jae b (Taken)\nx0010001100100101111 0001000000000111000 # jae c (Taken)\nx0010001100100111111 0001100000000111000 # jae d (Taken)\nx0010001100101001111 0010000000000111000 # jae e (Taken)\nx0010001100101011111 0010100000000111000 # jae bp (Taken)\nx0010001100101101111 0011000000000111000 # jae sp (Taken)\nx1010001100100001111 0000000000000111000 # jae a (Taken)\nx1010001100100011111 0000100000000111000 # jae b (Taken)\nx1010001100100101111 0001000000000111000 # jae c (Taken)\nx1010001100100111111 0001100000000111000 # jae d (Taken)\nx1010001100101001111 0010000000000111000 # jae e (Taken)\nx1010001100101011111 0010100000000111000 # jae bp (Taken)\nx1010001100101101111 0011000000000111000 # jae sp (Taken)\nxxx10001100100001111 0000000000001111000 # jae a (Skip)\nxxx10001100100011111 0000000000001111000 # jae b (Skip)\nxxx10001100100101111 0000000000001111000 # jae c (Skip)\nxxx10001100100111111 0000000000001111000 # jae d (Skip)\nxxx10001100101001111 0000000000001111000 # jae e (Skip)\nxxx10001100101011111 0000000000001111000 # jae bp (Skip)\nxxx10001100101101111 0000000000001111000 # jae sp (Skip)\nx0110001101000001111 0000000000000111000 # jl a (Taken)\nx0110001101000011111 0000100000000111000 # jl b (Taken)\nx0110001101000101111 0001000000000111000 # jl c (Taken)\nx0110001101000111111 0001100000000111000 # jl d (Taken)\nx0110001101001001111 0010000000000111000 # jl e (Taken)\nx0110001101001011111 0010100000000111000 # jl bp (Taken)\nx0110001101001101111 0011000000000111000 # jl sp (Taken)\nxxx10001101000001111 0000000000001111000 # jl a (Skip)\nxxx10001101000011111 0000000000001111000 # jl b (Skip)\nxxx10001101000101111 0000000000001111000 # jl c (Skip)\nxxx10001101000111111 0000000000001111000 # jl d (Skip)\nxxx10001101001001111 0000000000001111000 # jl e (Skip)\nxxx10001101001011111 0000000000001111000 # jl bp (Skip)\nxxx10001101001101111 0000000000001111000 # jl sp (Skip)\nx0110001101100001111 0000000000000111000 # jle a (Taken)\nx0110001101100011111 0000100000000111000 # jle b (Taken)\nx0110001101100101111 0001000000000111000 # jle c (Taken)\nx0110001101100111111 0001100000000111000 # jle d (Taken)\nx0110001101101001111 0010000000000111000 # jle e (Taken)\nx0110001101101011111 0010100000000111000 # jle bp (Taken)\nx0110001101101101111 0011000000000111000 # jle sp (Taken)\nx1010001101100001111 0000000000000111000 # jle a (Taken)\nx1010001101100011111 0000100000000111000 # jle b (Taken)\nx1010001101100101111 0001000000000111000 # jle c (Taken)\nx1010001101100111111 0001100000000111000 # jle d (Taken)\nx1010001101101001111 0010000000000111000 # jle e (Taken)\nx1010001101101011111 0010100000000111000 # jle bp (Taken)\nx1010001101101101111 0011000000000111000 # jle sp (Taken)\nxxx10001101100001111 0000000000001111000 # jle a (Skip)\nxxx10001101100011111 0000000000001111000 # jle b (Skip)\nxxx10001101100101111 0000000000001111000 # jle c (Skip)\nxxx10001101100111111 0000000000001111000 # jle d (Skip)\nxxx10001101101001111 0000000000001111000 # jle e (Skip)\nxxx10001101101011111 0000000000001111000 # jle bp (Skip)\nxxx10001101101101111 0000000000001111000 # jle sp (Skip)")) Instruction_Decorder (
    .in({and_5_out, shift_register_1_p5}),
    .out({Instruction_Decorder_out[18], Instruction_Decorder_out_2, Instruction_Decorder_out[13], shift_register_1_p6, Instruction_Decorder_out[9:0]}));
  not not_8 (not_8_out, Instruction_Decorder_out[18]);
  Adder #(.width(16)) adder_1 (
    .a(demultiplexer_2_out0), .b(demultiplexer_3_out0), .out(adder_1_out), .cout(adder_1_cout));  // open: cin
  Subtractor #(.width(16)) subtractor_1 (
    .a(demultiplexer_2_out1), .b(demultiplexer_3_out1), .out(subtractor_1_out), .bout(subtractor_1_bout[0]));  // open: bin
  Multiplier #(.width(16)) multiplier_1 (
    .a(demultiplexer_2_out2), .b(demultiplexer_3_out2), .out(multiplier_1_out), .cout(multiplier_1_cout));  // open: cin
  assign and_6_out = demultiplexer_2_out3 & demultiplexer_3_out3;  // AND_Gate and_6, 16 bits wide
  assign or_1_out = demultiplexer_2_out4 | demultiplexer_3_out4;  // OR_Gate or_1, 16 bits wide
  assign not_9_out = ~demultiplexer_2_out5;  // NOT_Gate not_9, 16 bits wide
  assign xor_1_out = demultiplexer_2_out6 ^ demultiplexer_3_out6;  // XOR_Gate xor_1, 16 bits wide
  D_Flip_Flop d_ff_2 (.D(and_5_out[16]), .clk(and_1_out), .Q(d_ff_2_q), .reset(RESET_out));  // open: Qn, preset
  LedBar #(.matrixcols(16)) ledbar_5 (
    .led0(multiplexer_17_out[15]), .led1(multiplexer_17_out[14]), .led2(multiplexer_17_out[13]),
    .led3(multiplexer_17_out[12]), .led4(multiplexer_17_out[11]), .led5(multiplexer_17_out[10]),
    .led6(multiplexer_17_out[9]), .led7(multiplexer_17_out[8]), .led8(multiplexer_17_out[7]),
    .led9(multiplexer_17_out[6]), .led10(multiplexer_17_out[5]), .led11(multiplexer_17_out[4]),
    .led12(multiplexer_17_out[3]), .led13(multiplexer_17_out[2]), .led14(multiplexer_17_out[1]),
    .led15(multiplexer_17_out[0]));
  Multiplexer #(.select(3), .width(16)) multiplexer_17 (
    .in0(adder_1_out), .in1(subtractor_1_out), .in2(multiplier_1_out), .in3(and_6_out), .in4(or_1_out),
    .in5(not_9_out), .in6(xor_1_out), .in7(undriven), .out(multiplexer_17_out),
    .sel(Instruction_Decorder_out[9:7]));
  or or_2 (subtractor_1_bout[2], adder_1_cout, multiplier_1_cout[0], multiplier_1_cout[1], multiplier_1_cout[2], multiplier_1_cout[3], multiplier_1_cout[4], multiplier_1_cout[5], multiplier_1_cout[6], multiplier_1_cout[7], multiplier_1_cout[8], multiplier_1_cout[9], multiplier_1_cout[10], multiplier_1_cout[11], multiplier_1_cout[12], multiplier_1_cout[13], multiplier_1_cout[14], multiplier_1_cout[15]);
  not not_10 (not_10_out, multiplexer_17_out[0]);
  not not_11 (not_11_out, multiplexer_17_out[1]);
  not not_12 (not_12_out, multiplexer_17_out[2]);
  not not_13 (not_13_out, multiplexer_17_out[3]);
  not not_14 (not_14_out, multiplexer_17_out[4]);
  not not_15 (not_15_out, multiplexer_17_out[5]);
  not not_16 (not_16_out, multiplexer_17_out[6]);
  not not_17 (not_17_out, multiplexer_17_out[7]);
  not not_18 (not_18_out, multiplexer_17_out[8]);
  not not_19 (not_19_out, multiplexer_17_out[9]);
  not not_20 (not_20_out, multiplexer_17_out[10]);
  not not_21 (not_21_out, multiplexer_17_out[11]);
  not not_22 (not_22_out, multiplexer_17_out[12]);
  not not_23 (not_23_out, multiplexer_17_out[13]);
  not not_24 (not_24_out, multiplexer_17_out[14]);
  not not_25 (not_25_out, multiplexer_17_out[15]);
  Register #(.width(16)) FLAGS (
    .D({{13{1'b0}}, subtractor_1_bout}), .en(1'b1), .clk(d_ff_2_q), .Q({FLAGS_q, and_5_out[19:17]}),
    .clr(RESET_out));
  and and_7 (subtractor_1_bout[1], not_17_out, not_10_out, not_11_out, not_12_out, not_13_out, not_14_out, not_15_out, not_16_out, not_18_out, not_19_out, not_20_out, not_21_out, not_22_out, not_23_out, not_24_out, not_25_out);

  // Notes on the sheet:
  //   REGISTERS
  //   石の数
endmodule

module div (
);

  wire adder_2_cout, adder_2_out, adder_3_cout, adder_4_cout, adder_4_out, adder_5_cout, adder_6_cout,
       adder_6_out, adder_7_cout, adder_8_cout, adder_8_out, dipswitch_1_p1, dipswitch_1_p2, dipswitch_1_p3,
       dipswitch_1_p4, dipswitch_1_p5, dipswitch_2_p1, dipswitch_2_p2, dipswitch_3_p1, dipswitch_3_p2,
       dipswitch_4_p1, dipswitch_4_p2, dipswitch_4_p3, dipswitch_4_p4, dipswitch_4_p5, dipswitch_4_p6,
       multiplexer_3_out, multiplexer_4_out, not_1_out, not_2_out, not_3_out, not_4_out, not_5_out,
       not_6_out, not_7_out, not_8_out;

  not not_1 (not_1_out, dipswitch_3_p1);
  // DipSwitch #(.number(4)) dipswitch_1: pin names not known; wires that end beside it: dipswitch_1_p1, dipswitch_1_p2, dipswitch_1_p3, dipswitch_1_p4, dipswitch_1_p5
  // DipSwitch #(.number(4)) dipswitch_2: pin names not known; wires that end beside it: dipswitch_2_p1, dipswitch_2_p2
  // NOT_Gate not_2 has open pins: in=open, out=not_2_out
  // NOT_Gate not_3 has open pins: in=open, out=not_3_out
  // NOT_Gate not_4 has open pins: in=open, out=not_4_out
  // NOT_Gate not_5 has open pins: in=open, out=not_5_out
  Multiplexer multiplexer_1 (.in0(dipswitch_1_p4), .in1(adder_2_out), .out(dipswitch_2_p1), .sel(adder_2_cout));
  // NOT_Gate not_6 has open pins: in=open, out=not_6_out
  Adder #(.width(1)) adder_1 (
    .a(not_1_out), .b(dipswitch_4_p1), .out(dipswitch_1_p5), .cin(adder_3_cout));  // open: cout
  Adder #(.width(1)) adder_2 (
    .a(not_5_out), .b(dipswitch_1_p4), .out(adder_2_out), .cin(adder_4_cout), .cout(adder_2_cout));
  // DipSwitch #(.number(4)) dipswitch_3: pin names not known; wires that end beside it: dipswitch_3_p1, dipswitch_3_p2
  // NOT_Gate not_7 has open pins: in=open, out=not_7_out
  // NOT_Gate not_8 has open pins: in=open, out=not_8_out
  Adder #(.width(1)) adder_3 (
    .a(not_6_out), .b(dipswitch_4_p2), .out(dipswitch_3_p2), .cin(adder_5_cout), .cout(adder_3_cout));
  Adder #(.width(1)) adder_4 (
    .a(not_4_out), .b(dipswitch_1_p3), .out(adder_4_out), .cin(adder_6_cout), .cout(adder_4_cout));
  Multiplexer multiplexer_2 (.in0(dipswitch_1_p3), .in1(adder_4_out), .out(dipswitch_2_p2), .sel(adder_2_cout));
  // DipSwitch #(.number(4)) dipswitch_4: pin names not known; wires that end beside it: dipswitch_4_p1, dipswitch_4_p2, dipswitch_4_p3, dipswitch_4_p4, dipswitch_4_p5, dipswitch_4_p6, dipswitch_1_p1, dipswitch_1_p2, dipswitch_1_p3, dipswitch_1_p4
  Adder #(.width(1)) adder_5 (
    .a(not_7_out), .b(dipswitch_4_p3), .out(dipswitch_4_p5), .cin(adder_7_cout), .cout(adder_5_cout));
  Adder #(.width(1)) adder_6 (
    .a(not_3_out), .b(dipswitch_1_p2), .out(adder_6_out), .cin(adder_8_cout), .cout(adder_6_cout));
  Multiplexer multiplexer_3 (.in0(dipswitch_1_p2), .in1(adder_6_out), .out(multiplexer_3_out), .sel(adder_2_cout));
  Adder #(.width(1)) adder_7 (.a(not_8_out), .b(dipswitch_4_p4), .out(dipswitch_4_p6), .cin(1'b1), .cout(adder_7_cout));
  Adder #(.width(1)) adder_8 (.a(not_2_out), .b(dipswitch_1_p1), .out(adder_8_out), .cin(1'b1), .cout(adder_8_cout));
  Multiplexer multiplexer_4 (.in0(dipswitch_1_p1), .in1(adder_8_out), .out(multiplexer_4_out), .sel(adder_2_cout));
endmodule
